// Logisim project alu.circ as structural Verilog: 1 circuit, main circuit alu
module alu (
  input  [31:0] A,
  input  [31:0] B,
  input  [3:0] ALUSel,
  output [31:0] ALUResult
);

  wire and_1_out, and_3_out, nand_1_out;
  wire [0:0] slt2;
  wire [31:0] add0, adder_1_out, and7, mul8, mulh9, mulhu11, multiplexer_1_out, not_1_out, or6, sll1, sra13,
       srl5, sub12, xor4;

  assign not_1_out = ~B;  // NOT_Gate not_1, 32 bits wide
  nand nand_1 (nand_1_out, ALUSel[0], ALUSel[1]);
  and and_1 (and_1_out, ALUSel[2], ALUSel[3]);
  Shifter #(.width(32)) shifter_1 (.in(A), .\dist (B[4:0]), .out(sll1));
  Comparator #(.width(32)) comparator_1 (.a(A), .b(B), .lt(slt2[0]));  // open: gt, eq
  assign or6 = A | B;  // OR_Gate or_1, 32 bits wide
  assign xor4 = A ^ B;  // XOR_Gate xor_1, 32 bits wide
  assign and7 = A & B;  // AND_Gate and_2, 32 bits wide
  Multiplier #(.mode("twosComplement"), .width(32)) multiplier_1 (.a(A), .b(B), .out(mul8));  // open: cin, cout
  Multiplier #(.width(32)) multiplier_2 (.a(A), .b(B), .cout(mulhu11));  // open: out, cin
  Multiplexer #(.width(32)) multiplexer_1 (.in0(B), .in1(not_1_out), .out(multiplexer_1_out), .sel(and_3_out));
  and and_3 (and_3_out, nand_1_out, and_1_out);
  Demultiplexer #(.width(32)) demultiplexer_1 (.out0(add0), .out1(sub12), .in(adder_1_out), .sel(and_3_out));
  Adder #(.width(32)) adder_1 (.a(A), .b(multiplexer_1_out), .out(adder_1_out), .cin(and_3_out));  // open: cout
  Shifter #(.shift("lr"), .width(32)) shifter_2 (.in(A), .\dist (B[4:0]), .out(srl5));
  Shifter #(.shift("ar"), .width(32)) shifter_3 (.in(A), .\dist (B[4:0]), .out(sra13));
  Multiplier #(.mode("twosComplement"), .width(32)) multiplier_3 (.a(A), .b(B), .cout(mulh9));  // open: out, cin
  Multiplexer #(.select(4), .width(32)) multiplexer_2 (
    .in0(add0), .in1(sll1), .in2({{31{1'b0}}, slt2[0]}), .in4(xor4), .in5(srl5), .in6(or6), .in7(and7),
    .in8(mul8), .in9(mulh9), .in11(mulhu11), .in12(sub12), .in13(sra13), .in15(B), .out(ALUResult),
    .sel(ALUSel));  // open: in3, in10, in14

  // Other names for the same wires on the sheet: bsel15[31:0] = B

  // Notes on the sheet:
  //   INPUTS to your circuit
  //   DON'T CHANGE THE LOCATIONS OF THE INPUTS AND OUTPUTS!
  //   OUTPUT from your circuit
endmodule
