// Logisim project cpu.circ as structural Verilog: 1 circuit, main circuit cpu
module cpu (
  input  clk,
  input  [31:0] Instruction,
  input  [31:0] MemReadData,
  output [31:0] MemAddress,
  output [31:0] ProgramCounter,
  output [31:0] ra,
  output [31:0] sp,
  output [31:0] t0,
  output [31:0] t1,
  output [31:0] t2,
  output [31:0] s0,
  output [31:0] s1,
  output [31:0] a0,
  output [3:0] MemWriteMask,
  output [31:0] MemWriteData
);

  wire Asel, BrEq, BrLt, BrUn, Bsel, MemWEn, PCSel, RegWEn, undriven;
  wire [1:0] WBSel;
  wire [2:0] func3, ImmSel;
  wire [3:0] ALUSel;
  wire [6:0] func7;
  wire [24:0] Instruction2;
  wire [31:0] adder_1_out, adder_2_out, Immediate, multiplexer_1_out, multiplexer_2_out, multiplexer_3_out,
       multiplexer_4_out, PC2, r1, r2, ReadData2, WriteData;

  Adder #(.width(32)) adder_1 (.a(ProgramCounter), .b(32'h4), .out(adder_1_out));  // open: cin, cout
  Multiplexer #(.width(32)) multiplexer_1 (.in0(adder_1_out), .in1(MemAddress), .out(multiplexer_1_out), .sel(PCSel));
  Register #(.width(32)) PC (.D(multiplexer_1_out), .clk(clk), .Q(ProgramCounter), .clr(undriven));  // open: en
  Multiplexer #(.width(32)) multiplexer_2 (.in0(Instruction), .in1(32'h13), .out(multiplexer_2_out), .sel(PCSel));
  Register #(.width(32)) register_1 (
    .D(multiplexer_2_out), .clk(clk), .Q({func7, Instruction2[24:15], func3, Instruction2[11:0]}));  // open: en, clr
  Register #(.width(32)) register_2 (.D(ProgramCounter), .clk(clk), .Q(PC2));  // open: en, clr
  control_logic control_logic_1 (
    .Instruction({func7, Instruction2[24:15], func3, Instruction2[11:0]}), .BrEq(BrEq), .BrLt(BrLt),
    .PCSel(PCSel), .RegWEn(RegWEn), .ImmSel(ImmSel), .BrUn(BrUn), .ASel(Asel), .BSel(Bsel), .ALUSel(ALUSel),
    .MemWEn(MemWEn), .WBSel(WBSel));
  regfile regfile_1 (
    .ReadIndex1(Instruction2[19:15]), .ReadIndex2(Instruction2[24:20]), .WriteIndex(Instruction2[11:7]),
    .WriteData(WriteData), .RegWEn(RegWEn), .clk(clk), .ra(ra), .sp(sp), .t0(t0), .t1(t1), .t2(t2), .s0(s0),
    .s1(s1), .a0(a0), .ReadData1(r1), .ReadData2(r2));
  imm_gen imm_gen_1 (
    .Instruction({func7, Instruction2[24:15], func3, Instruction2[11:0]}), .ImmSel(ImmSel),
    .Immediate(Immediate));
  Multiplexer #(.width(32)) multiplexer_3 (.in0(r2), .in1(Immediate), .out(multiplexer_3_out), .sel(Bsel));
  Multiplexer #(.width(32)) multiplexer_4 (.in0(r1), .in1(PC2), .out(multiplexer_4_out), .sel(Asel));
  alu alu_1 (.A(multiplexer_4_out), .B(multiplexer_3_out), .ALUSel(ALUSel), .ALUResult(MemAddress));
  branch_comp branch_comp_1 (.BrData1(r1), .BrData2(r2), .BrUn(BrUn), .BrEq(BrEq), .BrLt(BrLt));
  Adder #(.width(32)) adder_2 (.a(PC2), .b(32'h4), .out(adder_2_out));  // open: cin, cout
  Multiplexer #(.select(2), .width(32)) multiplexer_5 (
    .in0(ReadData2), .in1(MemAddress), .in2(adder_2_out), .in3(Immediate), .out(WriteData), .sel(WBSel));
  partial_store partial_store_1 (
    .Instruction({func7, Instruction2[24:15], func3, Instruction2[11:0]}), .MemAddress(MemAddress),
    .DataFromReg(r2), .MemWEn(MemWEn), .MemWriteMask(MemWriteMask), .DataToMem(MemWriteData));
  partial_load partial_load_1 (
    .Instruction({func7, Instruction2[24:15], func3, Instruction2[11:0]}), .MemAddress(MemAddress),
    .DataFromMem(MemReadData), .DataToReg(ReadData2));

  // Other names for the same wires on the sheet: ALURes[31:0] = MemAddress; opcode[6:0] = Instruction2[6:0];
  //   WriteReg[4:0] = Instruction2[11:7]; Instruction2 (some bits) = {func7, func3};
  //   ReadReg1[4:0] = Instruction2[19:15]; ReadReg2[4:0] = Instruction2[24:20]

  // Notes on the sheet:
  //   To IMEM
  //   IMEM (do **NOT** move this)
  //   Instruction Decode
  //   From IMEM
  //   Inputs/Outputs for testing. Do **NOT** move these.
  //   To DMEM
  //   DMEM (do **NOT** move this)
  //   From DMEM
endmodule
