// Logisim project partial-load.circ as structural Verilog: 1 circuit, main circuit partial_load
module partial_load (
  input  [31:0] Instruction,
  input  [31:0] MemAddress,
  input  [31:0] DataFromMem,
  output [31:0] DataToReg
);

  wire comparator_1_eq, comparator_2_eq, comparator_3_eq, comparator_4_eq, comparator_5_eq, comparator_6_eq,
       comparator_7_eq, comparator_8_eq, lb, lh, lw, sel0, sel1, sel2, sel3, selh0, selh1, selh2, selw;
  wire [1:0] multiplexer_5_out, multiplexer_6_out, multiplexer_7_out, multiplexer_8_out, selb, selh, selLoad;
  wire [31:0] bit_extender_1_out, bit_extender_2_out, bit_extender_3_out, bit_extender_4_out,
       bit_extender_5_out, bit_extender_6_out, bit_extender_7_out, multiplexer_1_out, multiplexer_2_out,
       multiplexer_3_out;

  Comparator #(.width(2)) comparator_1 (.a(MemAddress[1:0]), .b(2'b00), .eq(comparator_1_eq));  // open: gt, lt
  Comparator #(.width(2)) comparator_2 (.a(MemAddress[1:0]), .b(2'b01), .eq(comparator_2_eq));  // open: gt, lt
  Comparator #(.width(2)) comparator_3 (.a(MemAddress[1:0]), .b(2'b10), .eq(comparator_3_eq));  // open: gt, lt
  Comparator #(.width(2)) comparator_4 (.a(MemAddress[1:0]), .b(2'b11), .eq(comparator_4_eq));  // open: gt, lt
  assign bit_extender_1_out = {{24{DataFromMem[7]}}, DataFromMem[7:0]};  // Bit_Extender bit_extender_1
  assign bit_extender_2_out = {{24{DataFromMem[15]}}, DataFromMem[15:8]};  // Bit_Extender bit_extender_2
  assign bit_extender_3_out = {{24{DataFromMem[23]}}, DataFromMem[23:16]};  // Bit_Extender bit_extender_3
  assign bit_extender_4_out = {{24{DataFromMem[31]}}, DataFromMem[31:24]};  // Bit_Extender bit_extender_4
  and and_1 (sel0, lb, comparator_1_eq);
  and and_2 (sel1, lb, comparator_2_eq);
  and and_3 (sel2, lb, comparator_3_eq);
  and and_4 (sel3, lb, comparator_4_eq);
  Multiplexer #(.select(2), .width(32)) multiplexer_1 (
    .in0(bit_extender_1_out), .in1(bit_extender_2_out), .in2(bit_extender_3_out), .in3(bit_extender_4_out),
    .out(multiplexer_1_out), .sel(selb));
  Comparator #(.width(7)) comparator_5 (.a(Instruction[6:0]), .b(7'b0000011), .eq(comparator_5_eq));  // open: gt, lt
  and and_5 (selh0, lh, comparator_1_eq);
  and and_6 (selh1, lh, comparator_2_eq);
  and and_7 (selh2, lh, comparator_3_eq);
  assign bit_extender_5_out = {{16{DataFromMem[15]}}, DataFromMem[15:0]};  // Bit_Extender bit_extender_5
  assign bit_extender_6_out = {{16{DataFromMem[31]}}, DataFromMem[31:16]};  // Bit_Extender bit_extender_6
  assign bit_extender_7_out = {{16{DataFromMem[23]}}, DataFromMem[23:8]};  // Bit_Extender bit_extender_7
  Comparator #(.width(3)) comparator_6 (.a(Instruction[14:12]), .b(3'b000), .eq(comparator_6_eq));  // open: gt, lt
  Comparator #(.width(3)) comparator_7 (.a(Instruction[14:12]), .b(3'b001), .eq(comparator_7_eq));  // open: gt, lt
  Comparator #(.width(3)) comparator_8 (.a(Instruction[14:12]), .b(3'b010), .eq(comparator_8_eq));  // open: gt, lt
  and and_8 (selw, lw, comparator_1_eq);
  Multiplexer #(.select(2), .width(32)) multiplexer_2 (
    .in0(bit_extender_5_out), .in1(bit_extender_7_out), .in2(bit_extender_6_out), .out(multiplexer_2_out),
    .sel(selh));  // open: in3
  and and_9 (lb, comparator_5_eq, comparator_6_eq);
  Multiplexer #(.width(32)) multiplexer_3 (.in1(DataFromMem), .out(multiplexer_3_out), .sel(selw));  // open: in0
  and and_10 (lh, comparator_5_eq, comparator_7_eq);
  and and_11 (lw, comparator_5_eq, comparator_8_eq);
  Multiplexer #(.select(2), .width(32)) multiplexer_4 (
    .in0(multiplexer_1_out), .in1(multiplexer_2_out), .in2(multiplexer_3_out), .out(DataToReg), .sel(selLoad));  // open: in3
  Multiplexer #(.width(2)) multiplexer_5 (.in0(2'b00), .in1(2'b01), .out(multiplexer_5_out), .sel(sel1));
  Multiplexer #(.width(2)) multiplexer_6 (.in0(2'b00), .in1(2'b01), .out(multiplexer_6_out), .sel(selh1));
  Multiplexer #(.width(2)) multiplexer_7 (.in0(2'b00), .in1(2'b01), .out(multiplexer_7_out), .sel(lh));
  Multiplexer #(.width(2)) multiplexer_8 (.in0(multiplexer_5_out), .in1(2'b10), .out(multiplexer_8_out), .sel(sel2));
  Multiplexer #(.width(2)) multiplexer_9 (.in0(multiplexer_6_out), .in1(2'b10), .out(selh), .sel(selh2));
  Multiplexer #(.width(2)) multiplexer_10 (.in0(multiplexer_7_out), .in1(2'b10), .out(selLoad), .sel(lw));
  Multiplexer #(.width(2)) multiplexer_11 (.in0(multiplexer_8_out), .in1(2'b11), .out(selb), .sel(sel3));

  // Other names for the same wires on the sheet: opcode[6:0] = Instruction[6:0]; rd[4:0] = Instruction[11:7];
  //   func3[2:0] = Instruction[14:12]; rs1[4:0] = Instruction[19:15]; rs2[4:0] = Instruction[24:20];
  //   func7[6:0] = Instruction[31:25]

  // Notes on the sheet:
  //   INPUTS to your circuit
  //   DON'T CHANGE THE LOCATIONS OF THE INPUTS AND OUTPUTS!
  //   lw passes exactly DataFromMem
  //   lb
  //   lw
  //   lh
  //   OUTPUT from your circuit
endmodule
