// Logisim project partial-store.circ as structural Verilog: 1 circuit, main circuit partial_store
module partial_store (
  input  [31:0] Instruction,
  input  [31:0] MemAddress,
  input  [31:0] DataFromReg,
  input  MemWEn,
  output [3:0] MemWriteMask,
  output [31:0] DataToMem
);

  wire comparator_1_eq, comparator_2_eq, comparator_3_eq, comparator_4_eq, comparator_5_eq, comparator_6_eq,
       comparator_7_eq, comparator_8_eq, sb, sel0, sel1, sel2, sel3, selh, selh0, selh1, selw, sh, sw;
  wire [1:0] multiplexer_7_out, multiplexer_10_out, multiplexer_13_out, selb, selStore;
  wire [3:0] multiplexer_4_out, multiplexer_6_out, multiplexer_9_out, multiplexer_11_out, multiplexer_14_out,
       multiplexer_16_out;
  wire [31:0] bit_extender_1_out, bit_extender_2_out, bit_extender_3_out, bit_extender_4_out,
       multiplexer_1_out, multiplexer_2_out, multiplexer_3_out;

  Comparator #(.width(2)) comparator_1 (.a(MemAddress[1:0]), .b(2'b00), .eq(comparator_1_eq));  // open: gt, lt
  Comparator #(.width(2)) comparator_2 (.a(MemAddress[1:0]), .b(2'b01), .eq(comparator_2_eq));  // open: gt, lt
  Comparator #(.width(2)) comparator_3 (.a(MemAddress[1:0]), .b(2'b10), .eq(comparator_3_eq));  // open: gt, lt
  Comparator #(.width(2)) comparator_4 (.a(MemAddress[1:0]), .b(2'b11), .eq(comparator_4_eq));  // open: gt, lt
  and and_1 (sel0, sb, comparator_1_eq);
  and and_2 (sel1, sb, comparator_2_eq);
  and and_3 (sel2, sb, comparator_3_eq);
  and and_4 (sel3, sb, comparator_4_eq);
  assign bit_extender_1_out = {{24{1'b0}}, DataFromReg[7:0]};  // Bit_Extender bit_extender_1
  assign bit_extender_2_out = {{16{1'b0}}, {DataFromReg[7:0], {8{1'b0}}}};  // Bit_Extender bit_extender_2
  assign bit_extender_3_out = {{8{1'b0}}, {DataFromReg[7:0], {16{1'b0}}}};  // Bit_Extender bit_extender_3
  assign bit_extender_4_out = {{16{1'b0}}, DataFromReg[15:0]};  // Bit_Extender bit_extender_4
  Comparator #(.width(7)) comparator_5 (.a(Instruction[6:0]), .b(7'b0100011), .eq(comparator_5_eq));  // open: gt, lt
  Comparator #(.width(3)) comparator_6 (.a(Instruction[14:12]), .b(3'b000), .eq(comparator_6_eq));  // open: gt, lt
  Comparator #(.width(3)) comparator_7 (.a(Instruction[14:12]), .b(3'b001), .eq(comparator_7_eq));  // open: gt, lt
  Comparator #(.width(3)) comparator_8 (.a(Instruction[14:12]), .b(3'b010), .eq(comparator_8_eq));  // open: gt, lt
  Multiplexer #(.width(32)) multiplexer_1 (
    .in0(bit_extender_4_out), .in1({DataFromReg[15:0], {16{1'b0}}}), .out(multiplexer_1_out), .sel(selh));
  and and_5 (sb, comparator_5_eq, comparator_6_eq);
  and and_6 (sh, comparator_5_eq, comparator_7_eq);
  and and_7 (sw, comparator_5_eq, comparator_8_eq);
  and and_8 (selh0, sh, comparator_1_eq);
  and and_9 (selh1, sh, comparator_3_eq);
  Multiplexer #(.select(2), .width(32)) multiplexer_2 (
    .in0(bit_extender_1_out), .in1(bit_extender_2_out), .in2(bit_extender_3_out),
    .in3({DataFromReg[7:0], {24{1'b0}}}), .out(multiplexer_2_out), .sel(selb));
  Multiplexer #(.width(32)) multiplexer_3 (.in1(DataFromReg), .out(multiplexer_3_out), .sel(selw));  // open: in0
  and and_10 (selw, sw, comparator_1_eq);
  Multiplexer #(.width(4)) multiplexer_4 (.in0(4'b0000), .in1(4'b0001), .out(multiplexer_4_out), .sel(MemWEn));
  Multiplexer #(.select(2), .width(32)) multiplexer_5 (
    .in0(multiplexer_2_out), .in1(multiplexer_1_out), .in2(multiplexer_3_out), .out(DataToMem), .sel(selStore));  // open: in3
  Multiplexer #(.width(4)) multiplexer_6 (.in0(multiplexer_4_out), .in1(4'b0010), .out(multiplexer_6_out), .sel(sel1));
  Multiplexer #(.width(2)) multiplexer_7 (.in0(2'b00), .in1(2'b01), .out(multiplexer_7_out), .sel(sel1));
  Multiplexer multiplexer_8 (.in0(1'b0), .in1(1'b1), .out(selh), .sel(selh1));
  Multiplexer #(.width(4)) multiplexer_9 (.in0(multiplexer_6_out), .in1(4'b0100), .out(multiplexer_9_out), .sel(sel2));
  Multiplexer #(.width(2)) multiplexer_10 (.in0(multiplexer_7_out), .in1(2'b10), .out(multiplexer_10_out), .sel(sel2));
  Multiplexer #(.width(4)) multiplexer_11 (
    .in0(multiplexer_9_out), .in1(4'b1000), .out(multiplexer_11_out), .sel(sel3));
  Multiplexer #(.width(2)) multiplexer_12 (.in0(multiplexer_10_out), .in1(2'b11), .out(selb), .sel(sel3));
  Multiplexer #(.width(2)) multiplexer_13 (.in0(2'b00), .in1(2'b01), .out(multiplexer_13_out), .sel(sh));
  Multiplexer #(.width(4)) multiplexer_14 (
    .in0(multiplexer_11_out), .in1(4'b0011), .out(multiplexer_14_out), .sel(selh0));
  Multiplexer #(.width(2)) multiplexer_15 (.in0(multiplexer_13_out), .in1(2'b10), .out(selStore), .sel(sw));
  Multiplexer #(.width(4)) multiplexer_16 (
    .in0(multiplexer_14_out), .in1(4'b1100), .out(multiplexer_16_out), .sel(selh1));
  Multiplexer #(.width(4)) multiplexer_17 (.in0(multiplexer_16_out), .in1(4'b1111), .out(MemWriteMask), .sel(selw));

  // Other names for the same wires on the sheet: opcode[6:0] = Instruction[6:0]; rd[4:0] = Instruction[11:7];
  //   func3[2:0] = Instruction[14:12]; rs1[4:0] = Instruction[19:15]; rs2[4:0] = Instruction[24:20];
  //   func7[6:0] = Instruction[31:25]

  // Notes on the sheet:
  //   INPUTS to your circuit
  //   DON'T CHANGE THE LOCATIONS OF THE INPUTS AND OUTPUTS!
  //   OUTPUT from your circuit
  //   Instruction Decode
endmodule
