// Logisim project regfile.circ as structural Verilog: 1 circuit, main circuit regfile
module regfile (
  input  [4:0] ReadIndex1,
  input  [4:0] ReadIndex2,
  input  [4:0] WriteIndex,
  input  [31:0] WriteData,
  input  RegWEn,
  input  clk,
  output [31:0] ra,
  output [31:0] sp,
  output [31:0] t0,
  output [31:0] t1,
  output [31:0] t2,
  output [31:0] s0,
  output [31:0] s1,
  output [31:0] a0,
  output [31:0] ReadData1,
  output [31:0] ReadData2
);

  wire RegWE1, RegWE2, RegWE3, RegWE4, RegWE5, RegWE6, RegWE7, RegWE8, RegWE9, RegWE10, RegWE11, RegWE12,
       RegWE13, RegWE14, RegWE15, RegWE16, RegWE17, RegWE18, RegWE19, RegWE20, RegWE21, RegWE22, RegWE23,
       RegWE24, RegWE25, RegWE26, RegWE27, RegWE28, RegWE29, RegWE30, RegWE31;
  wire [31:0] x3, x4, x11, x12, x13, x14, x15, x16, x17, x18, x19, x20, x21, x22, x23, x24, x25, x26, x27,
       x28, x29, x30, x31;

  Register #(.width(32)) x1 (.D(WriteData), .en(RegWE1), .clk(clk), .Q(ra));  // open: clr
  Register #(.width(32)) register_1 (.D(WriteData), .en(RegWE2), .clk(clk), .Q(sp));  // open: clr
  Register #(.width(32)) register_2 (.D(WriteData), .en(RegWE3), .clk(clk), .Q(x3));  // open: clr
  Register #(.width(32)) register_3 (.D(WriteData), .en(RegWE4), .clk(clk), .Q(x4));  // open: clr
  Register #(.width(32)) register_4 (.D(WriteData), .en(RegWE5), .clk(clk), .Q(t0));  // open: clr
  Register #(.width(32)) register_5 (.D(WriteData), .en(RegWE6), .clk(clk), .Q(t1));  // open: clr
  Register #(.width(32)) register_6 (.D(WriteData), .en(RegWE7), .clk(clk), .Q(t2));  // open: clr
  Register #(.width(32)) register_7 (.D(WriteData), .en(RegWE8), .clk(clk), .Q(s0));  // open: clr
  Register #(.width(32)) register_8 (.D(WriteData), .en(RegWE9), .clk(clk), .Q(s1));  // open: clr
  Register #(.width(32)) register_9 (.D(WriteData), .en(RegWE10), .clk(clk), .Q(a0));  // open: clr
  Register #(.width(32)) register_10 (.D(WriteData), .en(RegWE11), .clk(clk), .Q(x11));  // open: clr
  Register #(.width(32)) register_11 (.D(WriteData), .en(RegWE12), .clk(clk), .Q(x12));  // open: clr
  Register #(.width(32)) register_12 (.D(WriteData), .en(RegWE13), .clk(clk), .Q(x13));  // open: clr
  Register #(.width(32)) register_13 (.D(WriteData), .en(RegWE14), .clk(clk), .Q(x14));  // open: clr
  Register #(.width(32)) register_14 (.D(WriteData), .en(RegWE15), .clk(clk), .Q(x15));  // open: clr
  Multiplexer #(.select(5), .width(32)) multiplexer_1 (
    .in0({32{1'b0}}), .in1(ra), .in2(sp), .in3(x3), .in4(x4), .in5(t0), .in6(t1), .in7(t2), .in8(s0),
    .in9(s1), .in10(a0), .in11(x11), .in12(x12), .in13(x13), .in14(x14), .in15(x15), .in16(x16), .in17(x17),
    .in18(x18), .in19(x19), .in20(x20), .in21(x21), .in22(x22), .in23(x23), .in24(x24), .in25(x25),
    .in26(x26), .in27(x27), .in28(x28), .in29(x29), .in30(x30), .in31(x31), .out(ReadData1), .sel(ReadIndex1));
  Register #(.width(32)) register_15 (.D(WriteData), .en(RegWE16), .clk(clk), .Q(x16));  // open: clr
  Register #(.width(32)) register_16 (.D(WriteData), .en(RegWE17), .clk(clk), .Q(x17));  // open: clr
  Register #(.width(32)) register_17 (.D(WriteData), .en(RegWE18), .clk(clk), .Q(x18));  // open: clr
  Register #(.width(32)) register_18 (.D(WriteData), .en(RegWE19), .clk(clk), .Q(x19));  // open: clr
  Register #(.width(32)) register_19 (.D(WriteData), .en(RegWE20), .clk(clk), .Q(x20));  // open: clr
  Register #(.width(32)) register_20 (.D(WriteData), .en(RegWE21), .clk(clk), .Q(x21));  // open: clr
  Register #(.width(32)) register_21 (.D(WriteData), .en(RegWE22), .clk(clk), .Q(x22));  // open: clr
  Register #(.width(32)) register_22 (.D(WriteData), .en(RegWE23), .clk(clk), .Q(x23));  // open: clr
  Register #(.width(32)) register_23 (.D(WriteData), .en(RegWE24), .clk(clk), .Q(x24));  // open: clr
  Register #(.width(32)) register_24 (.D(WriteData), .en(RegWE25), .clk(clk), .Q(x25));  // open: clr
  Register #(.width(32)) register_25 (.D(WriteData), .en(RegWE26), .clk(clk), .Q(x26));  // open: clr
  Register #(.width(32)) register_26 (.D(WriteData), .en(RegWE27), .clk(clk), .Q(x27));  // open: clr
  Register #(.width(32)) register_27 (.D(WriteData), .en(RegWE28), .clk(clk), .Q(x28));  // open: clr
  Register #(.width(32)) register_28 (.D(WriteData), .en(RegWE29), .clk(clk), .Q(x29));  // open: clr
  Register #(.width(32)) register_29 (.D(WriteData), .en(RegWE30), .clk(clk), .Q(x30));  // open: clr
  Register #(.width(32)) register_30 (.D(WriteData), .en(RegWE31), .clk(clk), .Q(x31));  // open: clr
  Multiplexer #(.select(5), .width(32)) multiplexer_2 (
    .in0({32{1'b0}}), .in1(ra), .in2(sp), .in3(x3), .in4(x4), .in5(t0), .in6(t1), .in7(t2), .in8(s0),
    .in9(s1), .in10(a0), .in11(x11), .in12(x12), .in13(x13), .in14(x14), .in15(x15), .in16(x16), .in17(x17),
    .in18(x18), .in19(x19), .in20(x20), .in21(x21), .in22(x22), .in23(x23), .in24(x24), .in25(x25),
    .in26(x26), .in27(x27), .in28(x28), .in29(x29), .in30(x30), .in31(x31), .out(ReadData2), .sel(ReadIndex2));
  Demultiplexer #(.select(5)) demultiplexer_1 (
    .out1(RegWE1), .out2(RegWE2), .out3(RegWE3), .out4(RegWE4), .out5(RegWE5), .out6(RegWE6), .out7(RegWE7),
    .out8(RegWE8), .out9(RegWE9), .out10(RegWE10), .out11(RegWE11), .out12(RegWE12), .out13(RegWE13),
    .out14(RegWE14), .out15(RegWE15), .out16(RegWE16), .out17(RegWE17), .out18(RegWE18), .out19(RegWE19),
    .out20(RegWE20), .out21(RegWE21), .out22(RegWE22), .out23(RegWE23), .out24(RegWE24), .out25(RegWE25),
    .out26(RegWE26), .out27(RegWE27), .out28(RegWE28), .out29(RegWE29), .out30(RegWE30), .out31(RegWE31),
    .in(RegWEn), .sel(WriteIndex));  // open: out0

  // Other names for the same wires on the sheet: x1[31:0] = ra; x2[31:0] = sp; x5[31:0] = t0; x6[31:0] = t1;
  //   x7[31:0] = t2; x8[31:0] = s0; x9[31:0] = s1; x10[31:0] = a0

  // Notes on the sheet:
  //   INPUTS to your circuit
  //   DON'T CHANGE THE LOCATIONS OF THE INPUTS AND OUTPUTS!
  //   These are DEBUG/TEST outputs from your circuit.
  //   OUTPUTS from your circuit
endmodule
